# Fritzing sketch 02-potentiometer (saved by Fritzing 0.9.1b)
breadboards: 1

parts:
  Part1 = Arduino Uno (Rev3) - ICSP
  R1 = Rotary Potentiometer (Small) [maximum_resistance=100kΩ package=THT]
  LED1 = smd LED [color="Red (633nm)" package="1206 [SMD]"]
  R2 = Resistor [tolerance=±5% resistance=220 package=THT]

nets:
  N1: Part1.5V, R1.leg2
  N2: Part1.GND, R1.leg1, R2.Pin_0
  N3: R1.wiper, LED1.anode
  N4: LED1.cathode, R2.Pin_1
