# Fritzing sketch 03-color-led (saved by Fritzing 0.9.1b)
breadboards: 1

parts:
  Part1 = Arduino Ethernet Shield (Rev3)
  LED1 = RGB LED - (4 legs) [package="5 mm [THT]"]
  R1 = Resistor [tolerance=±5% resistance=220 package=THT]
  R2 = Resistor [tolerance=±5% resistance=220 package=THT]
  R3 = Resistor [tolerance=±5% resistance=220 package=THT]

nets:
  N1: Part1.PWM_D9, R3.Pin_1
  N2: Part1.ETH_CS, R2.Pin_1
  N3: Part1.PWM_D11, R1.Pin_1
  N4: Part1.GND, LED1.green_cathode
  N5: LED1.red_cathode, R1.Pin_0
  N6: LED1.common_anode, R2.Pin_0
  N7: LED1.blue_cathode, R3.Pin_0
